# Fritzing sketch Pi Circuit (saved by Fritzing 0.9.3b)
breadboards: 1

parts:
  Raspberry_Pi_1 = Raspberry Pi 3 [part_number=RPI-3-V1.2]
  DHT1 = DHT11 Humitidy and Temperature Sensor
  R1 = Resistor [tolerance=±5% resistance=10k package=THT]
  J1 = Piezo Speaker

nets:
  3V3: Raspberry_Pi_1.3v3, DHT1.VDD, R1.Pin_0
  N1: Raspberry_Pi_1.GPIO2, J1.pin2
  N2: Raspberry_Pi_1.GIPO4, DHT1.DATA, R1.Pin_1
  GND: Raspberry_Pi_1.GND, DHT1.GND, J1.pin1

custom parts:
  DHT11 Humitidy and Temperature Sensor: DHT11 Humidity and Temperature Sensor
